# Fritzing sketch escornabot_ultrasonidos (saved by Fritzing 0.9.3b)
breadboards: 1

parts:
  MOTOR1 = 28BYJ-48 Stepper Motor
  BREAKOUT1 = ULN2003A breakout board
  Componente1 = Arduino Nano (Rev3.0) (ICSP)
  MOTOR2 = 28BYJ-48 Stepper Motor
  BREAKOUT2 = ULN2003A breakout board
  VCC1 = 4 x AAA Battery Mount
  hc-sr1 = hc-sr04
  J1 = Piezo Speaker

nets:
  N1: MOTOR1.RED, BREAKOUT1.RED_wire
  N2: MOTOR1.ORANGE, BREAKOUT1.ORANGE_wire
  N3: MOTOR1.YELLOW, BREAKOUT1.YELLOW_wire
  N4: MOTOR1.PINK, BREAKOUT1.PINK_wire
  N5: MOTOR1.BLUE, BREAKOUT1.BLUE_wire
  N6: BREAKOUT1.In_1, Componente1.D9
  N7: BREAKOUT1.In_2, Componente1.D8
  N8: BREAKOUT1.In_3, Componente1.D7
  N9: BREAKOUT1.In_4, Componente1.D6
  GND: BREAKOUT1.0V, Componente1.GND, BREAKOUT2.0V, VCC1.-, hc-sr1.GND, J1.pin1
  +5V: BREAKOUT1.+5V, Componente1.VIN, BREAKOUT2.+5V, VCC1.+
  N10: Componente1.D2, BREAKOUT2.In_4
  N11: Componente1.D3, BREAKOUT2.In_3
  N12: Componente1.D4, BREAKOUT2.In_2
  N13: Componente1.D5, BREAKOUT2.In_1
  N14: Componente1.D10, J1.pin2
  N15: Componente1.D11/MOSI, hc-sr1.Trig
  N16: Componente1.D12/MISO, hc-sr1.Echo
  5V: Componente1.5V, hc-sr1.VCC
  N17: MOTOR2.RED, BREAKOUT2.RED_wire
  N18: MOTOR2.ORANGE, BREAKOUT2.ORANGE_wire
  N19: MOTOR2.YELLOW, BREAKOUT2.YELLOW_wire
  N20: MOTOR2.PINK, BREAKOUT2.PINK_wire
  N21: MOTOR2.BLUE, BREAKOUT2.BLUE_wire

custom parts:
  ULN2003A breakout board: ULN2003A 7-way Darlington Transistor Driver on breakoutboard
